# Fritzing sketch jaleometro_v1_5 (saved by Fritzing 1.0.1rc)

parts:
  Mod2 = Heltec CubeCell Dev-Board [part_number=HTCC-AB01]
  Solar_Panel = Solar Cell
  SparkFun_Sound_Detector = Sound Detector
  U1 = Battery Holders [package=lipo-1100mAh]
  J4 = Camdenboss CTB0158-2 [part_number=CTB0158-2 package=THT]
  J5 = Camdenboss CTB0158-5 [part_number=CTB0158-5 package=THT]
  J7 = Camdenboss CTB0158-2 [part_number=CTB0158-2 package=THT]

nets:
  N1: Mod2.pin1, J5.pin4
  N2: Mod2.pin_11, Mod2.pin_14, Mod2.pin_18, J4.pin1, J5.pin1
  N3: Mod2.pin_15, J4.pin2
  N4: Mod2.pin_17, J5.pin2
  N5: Solar_Panel.+, J4.terminal_2
  N6: Solar_Panel.-, J4.terminal_1
  N7: SparkFun_Sound_Detector.AUDIO, J5.terminal_5
  N8: SparkFun_Sound_Detector.ENVELOPE, J5.terminal_4
  N9: SparkFun_Sound_Detector.GATE, J5.terminal_3
  N10: SparkFun_Sound_Detector.VCC, J5.terminal_2
  N11: SparkFun_Sound_Detector.GND, J5.terminal_1
  N12: U1.+, J7.terminal_2
  N13: U1.-, J7.terminal_1

custom parts:
  Heltec CubeCell Dev-Board: CubeCell is a part of the Heltec LoRa series and incorporates a PSoC 4000 series processor and SX1262 RF transceiver with an integrated CP2102 USB to serial port interface and onboard SHT1.25 battery interface with integrated lithium battery management system, supporting direct solar panel connection. Links: Heltec CubeCell Dev-Board product page Github
  Sound Detector: Electret microphone with multiple outputs. - First output is the actual audio - Second output is the amplitude envelope - Third output is a binary "sound present" indication - high while sound is present, low otherwise. Visit sparkfun.com for more documentations.
